# Fritzing sketch FreezerThermometer (saved by Fritzing 0.9.1b)
breadboards: 1

parts:
  LCD1 = Adafruit Negative RGB 2x16 LCD
  U1 = TMP36 [package=to-92-kit]
  RedBoard1 = RedBoard [part_number=DEV-11575]

nets:
  VCC: LCD1.no_name_yet#3, U1.VCC, RedBoard1.aref, RedBoard1.3V3
  GND: LCD1.no_name_yet#6, U1.GND, RedBoard1.GND
  N1: LCD1.no_name_yet#12, RedBoard1.A4
  N2: LCD1.no_name_yet#13, RedBoard1.A5
  N3: U1.VOUT, RedBoard1.A1

custom parts:
  Adafruit Negative RGB 2x16 LCD: Adafruit Negative 2x16 LCD Display with RGB Backlight
  RedBoard: At SparkFun we use many Arduinos and we're always looking for the simplest, most stable one. Each board is a bit different and no one board has everything we want, so we decided to make our own version that combines all our favorite features. The RedBoard combines the simplicity of the UNO's Optiboot bootloader (which is used in the Pro series), the stability of the FTDI (which we all missed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
